# Fritzing sketch P-Light (saved by Fritzing 0.9.3b)
breadboards: 1

parts:
  U1 = Voltage Regulator - 5V [package="TO220 [THT]"]
  R1 = Resistor [tolerance=±1% resistance=470 package=THT]
  R2 = Resistor [tolerance=±1% resistance=10 package=THT]
  C1 = Electrolytic Capacitor [capacitance=1µF package="100 mil [THT, electrolytic]"]
  C2 = Ceramic Capacitor [capacitance=100nF package="200 mil [THT, multilayer]"]
  C3 = Tantalum Capacitor [capacitance=10µF package="200 mil [THT, tantalum]"]
  C4 = Ceramic Capacitor [capacitance=100nF package="200 mil [THT, multilayer]"]
  J1 = Screw terminal - 2 pins [package=THT]
  Q1 = TIP120 Hi-Current Darlington Transistor
  R3 = Resistor [tolerance=±1% resistance=2.7k package=THT]
  Q2 = TIP120 Hi-Current Darlington Transistor
  Q3 = TIP120 Hi-Current Darlington Transistor
  R4 = Resistor [tolerance=±1% resistance=2.7k package=THT]
  R5 = Resistor [tolerance=±1% resistance=2.7k package=THT]
  J2 = screw terminal, 4 pins
  J3 = female pin header, 6 pins [form="♀ (female)"]
  R6 = Resistor [tolerance=±1% resistance=10k package=THT]
  R7 = Resistor [tolerance=±1% resistance=10k package=THT]
  R8 = Resistor [tolerance=±1% resistance=10k package=THT]
  R9 = Resistor [tolerance=±1% resistance=10k package=THT]
  C5 = Electrolytic Capacitor [capacitance=1µF package="100 mil [THT, electrolytic]"]
  C6 = Ceramic Capacitor [capacitance=100nF package="100 mil [THT, multilayer]"]
  U2 = ESP8266 WiFi Module [part_number=ESP8266]
  U3 = V_REG_LD1117VXX [package=78xxl]
  S1 = SWITCH-MOMENTARY-2 [package=tactile-pth]

nets:
  N1: U1.input_voltage, C1.+, C2.1, J1.pin2, J2.pin1
  N2: U1.GND, R1.Pin_1, R2.Pin_1
  N3: U1.output_voltage, R1.Pin_0, C3.+, C4.0, U3.IN
  GND: R2.Pin_0, C1.-, C2.0, C3.-, C4.1, J1.pin1, Q1.EMITTER, Q2.EMITTER, Q3.EMITTER, J3.pin6, R9.Pin_1, C5.-, C6.0, U2.GND, U3.GND, S1.2
  N4: Q1.BASE, R3.Pin_1
  N5: Q1.COLLECTOR, J2.pin2
  N6: R3.Pin_0, U2.GPIO_13
  N7: Q2.BASE, R4.Pin_1
  N8: Q2.COLLECTOR, J2.pin3
  N9: Q3.BASE, R5.Pin_1
  N10: Q3.COLLECTOR, J2.pin4
  N11: R4.Pin_0, U2.GPIO_12
  N12: R5.Pin_0, U2.GPIO_14
  N13: J3.pin1, U2.RXD
  N14: J3.pin2, U2.TXD
  N15: J3.pin3, R8.Pin_1, U2.REST, S1.1
  N16: J3.pin4, R7.Pin_1, U2.GPIO_0
  N17: J3.pin5, R6.Pin_0, R7.Pin_0, R8.Pin_0, C5.+, C6.1, U2.VCC, U3.OUT
  N18: R6.Pin_1, U2.CH_PD
  N19: R9.Pin_0, U2.GPIO_15

custom parts:
  SWITCH-MOMENTARY-2: Various NO switches- pushbuttons, reed, etc
