# Fritzing sketch TestAtTynih (saved by Fritzing 0.9.3b)
breadboards: 1

parts:
  Raspberry_Pi_1 = Raspberry Pi 3 [part_number=RPI-3-V1.2]
  J1 = Screw terminal - 2 pins [package=THT]
  R1 = Resistor [tolerance=±5% resistance=220 package=THT]
  R2 = Resistor [tolerance=±5% resistance=330 package=THT]
  J2 = Screw terminal - 2 pins [package=THT]
  U1 = attiny85 [package=dip]
  LED2 = LED - 3mm [color="Green (560nm)" package="3 mm [THT]"]  # not connected
  LED1 = LED - 3mm [color="Red (633nm)" package="3 mm [THT]"]  # not connected
  J3 = screw terminal, 5 pins
  R3 = Resistor [tolerance=±5% resistance=220 package=THT]

nets:
  N1: Raspberry_Pi_1.GND, J1.pin1, U1.Pin_4
  N2: Raspberry_Pi_1.GPIO19, U1.Pin_3
  N3: Raspberry_Pi_1.GPIO26, U1.Pin_2, R3.Pin_1
  N4: J1.pin2, U1.Pin_8, J3.pin1
  N5: R1.Pin_0, J2.pin2
  N6: R1.Pin_1, U1.Pin_7
  N7: R2.Pin_1, J2.pin1
  N8: U1.Pin_5, J3.pin3
  N9: U1.Pin_6, J3.pin4
  N10: J3.pin2, R3.Pin_0
