# Fritzing sketch polelighttest (saved by Fritzing 0.9.3b)
breadboards: 1

parts:
  Power_plug1 = Power plug
  U1 = Voltage Regulator - 5V [package="TO220 [THT]"]
  C4 = Electrolytic Capacitor [capacitance=2.2mF voltage=16V package="100 mil [THT, electrolytic]"]
  R2 = Resistor [tolerance=±1% resistance=10 package=THT]
  R1 = Resistor [tolerance=±1% resistance=470 package=THT]
  C2 = Ceramic Capacitor [capacitance=100nF package="200 mil [THT, multilayer]"]
  C1 = Ceramic Capacitor [capacitance=100nF package="200 mil [THT, multilayer]"]
  C5 = Tantalum Capacitor [capacitance=10µF package="200 mil [THT, tantalum]"]

nets:
  N1: Power_plug1.GND, C4.-, R2.Pin_0, C2.0, C1.1, C5.-
  N2: Power_plug1.VCC, U1.input_voltage, C4.+, C2.1
  N3: U1.GND, R2.Pin_1, R1.Pin_1
  N4: U1.output_voltage, R1.Pin_0, C1.0, C5.+
